# Fritzing sketch Morse_Code_Translator (saved by Fritzing 0.9.3b)
breadboards: 1

parts:
  Part1 = Arduino Nano (Rev3.0) (ICSP)
  IC1 = KS0232 [chip_label=?]
  Part3 = KY-006 Passive Buzzer Module [package="Breakout board"]

nets:
  GND: Part1.GND, IC1.GND, Part3.-
  N1: Part1.D2, Part3.S
  5V: Part1.5V, IC1.VCC

notes:
  Morse Code Translator

custom parts:
  KS0232: Led red
  KY-006 Passive Buzzer Module: Passive Piezoelectric Buzzer Module Keyes KY-006, it can produce a range of sound tones depending on the input frequency.
